# Fritzing sketch SXEDIO_KYKLWMATOS (saved by Fritzing 0.8.7b)
breadboards: 2

parts:
  Εξάρτημα1 = Arduino Mega 2560 (Rev3)
  LED1 = LED - 5mm [color="White (4500K)" package="5 mm [THT]"]
  R1 = Photocell (LDR) [package=THT]
  DHT22 = Humidity and Temperature Sensor RHT03
  R2 = Resistor [tolerance=±5% resistance=220 package=THT]
  R4 = Resistor 10K [package="0402 [SMD]"]
  PIR1 = PIR sensor
  Εξάρτημα2 = FC-28 Soil Hygrometer Module - Probe
  R5 = Photocell (LDR) [package=THT]
  R6 = Resistor 10K [package="0402 [SMD]"]
  Εξάρτημα3 = FC-28 Soil Hygrometer Module
  R7 = Resistor 10K [package="0402 [SMD]"]
  M1 = DC Motor
  KY-1 = Keyes Relay [package=THT]
  Part2 = Solar Panel [package="Renogy 50 Watts 12 Volt Monocrystalline Bendable Solar Panel"]  # not connected
  BAT2 = Battery Holders [package=lipo-1100mAh]

nets:
  N1: Εξάρτημα1.A0, R1.pin_0, R4.Pin_1
  N2: Εξάρτημα1.A1, Εξάρτημα3.AO
  N3: Εξάρτημα1.A2, R5.pin_0, R6.Pin_1
  N4: Εξάρτημα1.D13_PWM, KY-1.signal
  5V: Εξάρτημα1.5V, R1.pin_1, PIR1.VDD
  GND: Εξάρτημα1.GND, LED1.cathode, DHT22.GND_2, R4.Pin_0, PIR1.GND, R6.Pin_0, Εξάρτημα3.GND, KY-1.ground
  N5: Εξάρτημα1.D3_PWM, R2.Pin_1
  N6: Εξάρτημα1.D4_PWM, PIR1.SIG
  N7: LED1.anode, R2.Pin_0
  N8: DHT22.Data-signal, R7.Pin_0
  N9: Εξάρτημα2.POS, Εξάρτημα3.POS
  N10: Εξάρτημα2.NEG, Εξάρτημα3.NEG
  N11: R5.pin_1, Εξάρτημα3.VCC, R7.Pin_1, KY-1.power
  N12: M1.pin_1, KY-1.NO
  N13: KY-1.C, BAT2.+

notes:
  VCC
  GND
  Solar Panel battery Charger V 1.0
  Η μπαταρία με τη βοήθεια κατάλληληςθήκης και καλωδίου τροφοδοτεί με ρεύμα επίσης το Arduino
  Step up booster 5Volt.
  Αιρθητήρας Κίνησης
  Τρόμπα νερού
  Ρελέ
  Αισθητήρας υγρασίας εδάφους

custom parts:
  Resistor 10K: Resistor Basic schematic elements and footprints for 0603, 1206, and PTH resistors.
  FC-28 Soil Hygrometer Module - Probe: The FC-28 is a soil hygrometer module that uses the Texas Instruments LM393 comparator chip to provide an analog measurement of soil humidity.
  FC-28 Soil Hygrometer Module: The FC-28 is a soil hygrometer module that uses the Texas Instruments LM393 comparator chip to provide an analog measurement of soil humidity. The digital output is high when soil moisture is over a certain threshold, as determined by adjusting the potentiometer.
  DC Motor: Your standard DC Motor
  Keyes Relay: The Keyes 5V relay module is suitable for SCM development, home appliance control. It uses a 5V~12V TIL control signal which can control DC / AC signal.
  Solar Panel: 3,5 Watts 6 Volt Solar Panel
